# Fritzing sketch stampede (saved by Fritzing 0.9.2b)
breadboards: 1

parts:
  S1 = SWITCH-MOMENTARY-2 [package=tactile-pth-12mm]
  MCU = Arduino Uno (Rev3)
  S2 = SWITCH-MOMENTARY-2 [package=tactile-pth-12mm]
  S3 = SWITCH-MOMENTARY-2 [package=tactile-pth-12mm]
  S4 = SWITCH-MOMENTARY-2 [package=tactile-pth-12mm]
  S6 = SWITCH-MOMENTARY-2 [package=tactile-pth-12mm]
  S5 = SWITCH-MOMENTARY-2 [package=tactile-pth-12mm]
  S8 = SWITCH-MOMENTARY-2 [package=tactile-pth-12mm]
  S7 = SWITCH-MOMENTARY-2 [package=tactile-pth-12mm]
  PortExpander = SSOP28DB [chip_label=MCP23017 package=SSOP]
  S_Edit = SWITCH-MOMENTARY-2 [package=tactile-pth-12mm]
  S_Bypass = SWITCH-MOMENTARY-2 [package=tactile-pth-12mm]
  LED_1 = LEDs [package=led10mm]
  LED_2 = LEDs [package=led10mm]
  LED_3 = LEDs [package=led10mm]
  LED_4 = LEDs [package=led10mm]
  LED_5 = LEDs [package=led10mm]
  LED_8 = LEDs [package=led10mm]
  LED_7 = LEDs [package=led10mm]
  LED_6 = LEDs [package=led10mm]
  LED_Edit = LEDs [package=led10mm]
  LED_Bypass = LEDs [package=led10mm]
  U2 = RELAY [package=relay-t9a]
  U3 = RELAY [package=relay-t9a]
  U4 = RELAY [package=relay-t9a]
  U5 = RELAY [package=relay-t9a]
  U6 = RELAY [package=relay-t9a]
  U7 = RELAY [package=relay-t9a]
  U8 = RELAY [package=relay-t9a]
  U9 = RELAY [package=relay-t9a]
  U10 = 2.5mm Audio Jack [package=stereojack2.5mm_smd]
  U11 = 2.5mm Audio Jack [package=stereojack2.5mm_smd]
  U12 = 2.5mm Audio Jack [package=stereojack2.5mm_smd]
  U13 = 2.5mm Audio Jack [package=stereojack2.5mm_smd]
  U14 = 2.5mm Audio Jack [package=stereojack2.5mm_smd]
  U15 = 2.5mm Audio Jack [package=stereojack2.5mm_smd]
  U16 = 2.5mm Audio Jack [package=stereojack2.5mm_smd]
  U17 = 2.5mm Audio Jack [package=stereojack2.5mm_smd]
  U18 = 2.5mm Audio Jack [package=stereojack2.5mm_smd]
  U19 = 2.5mm Audio Jack [package=stereojack2.5mm_smd]
  U20 = 2.5mm Audio Jack [package=stereojack2.5mm_smd]
  U21 = 2.5mm Audio Jack [package=stereojack2.5mm_smd]
  U22 = 2.5mm Audio Jack [package=stereojack2.5mm_smd]
  U23 = 2.5mm Audio Jack [package=stereojack2.5mm_smd]
  U24 = 2.5mm Audio Jack [package=stereojack2.5mm_smd]
  U25 = 2.5mm Audio Jack [package=stereojack2.5mm_smd]
  U26 = RELAY [package=relay-t9a]
  U27 = RELAY [package=relay-t9a]
  U28 = RELAY [package=relay-t9a]
  U29 = RELAY [package=relay-t9a]
  U30 = RELAY [package=relay-t9a]
  U31 = RELAY [package=relay-t9a]
  U32 = RELAY [package=relay-t9a]
  U33 = RELAY [package=relay-t9a]
  U34 = 2.5mm Audio Jack [package=stereojack2.5mm_smd]
  U35 = 2.5mm Audio Jack [package=stereojack2.5mm_smd]
  R1 = Resistor [tolerance=±5% resistance=220 package="0402 [SMD]"]
  R2 = Resistor [tolerance=±5% resistance=220 package="0402 [SMD]"]
  R3 = Resistor [tolerance=±5% resistance=220 package="0402 [SMD]"]
  R4 = Resistor [tolerance=±5% resistance=220 package="0402 [SMD]"]
  R5 = Resistor [tolerance=±5% resistance=220 package="0402 [SMD]"]
  R6 = Resistor [tolerance=±5% resistance=220 package="0402 [SMD]"]
  R7 = Resistor [tolerance=±5% resistance=220 package="0402 [SMD]"]
  R8 = Resistor [tolerance=±5% resistance=220 package="0402 [SMD]"]
  R9 = Resistor [tolerance=±5% resistance=220 package="0402 [SMD]"]
  R10 = Resistor [tolerance=±5% resistance=220 package="0402 [SMD]"]

nets:
  N1: S1.1, MCU.D0/RX
  N2: MCU.A4/SDA, PortExpander.13
  N3: MCU.D8, S_Edit.1
  N4: MCU.D9_PWM, S_Bypass.1
  N5: MCU.A5/SCL, PortExpander.12
  N6: MCU.D1/TX, S2.1
  N7: MCU.D2, S3.1
  N8: MCU.D3_PWM, S4.1
  N9: MCU.D4, S5.1
  N10: MCU.D5_PWM, S6.1
  N11: MCU.D6_PWM, S7.1
  N12: MCU.D7, S8.1
  N13: PortExpander.4, U27.COIL1, U31.COIL1
  N14: PortExpander.5, U28.COIL1, U32.COIL1
  N15: PortExpander.6, U29.COIL1, U30.COIL1
  N16: PortExpander.7, U26.COIL1, U33.COIL1
  N17: PortExpander.8, U8.COIL1, U9.COIL1
  N18: PortExpander.9, U6.COIL1, U7.COIL1
  N19: PortExpander.10, U4.COIL1, U5.COIL1
  N20: PortExpander.11, U2.COIL1, U3.COIL1
  N21: PortExpander.19, R1.Pin_0
  N22: PortExpander.20, R2.Pin_0
  N23: PortExpander.21, R3.Pin_0
  N24: PortExpander.22, R4.Pin_0
  N25: PortExpander.23, R5.Pin_0
  N26: PortExpander.24, R7.Pin_0
  N27: PortExpander.25, R6.Pin_0
  N28: PortExpander.26, R8.Pin_0
  N29: PortExpander.27, R9.Pin_0
  N30: PortExpander.28, R10.Pin_0
  GND: S_Bypass.2, LED_1.C, LED_2.C, LED_3.C, LED_4.C, LED_5.C, LED_8.C, LED_7.C, LED_6.C, LED_Edit.C, LED_Bypass.C, U2.COIL2, U3.COIL2, U4.COIL2, U5.COIL2, U6.COIL2, U7.COIL2, U8.COIL2, U9.COIL2, U26.COIL2, U27.COIL2, U28.COIL2, U29.COIL2, U30.COIL2, U31.COIL2, U32.COIL2, U33.COIL2
  N31: LED_1.A, R1.Pin_1
  N32: LED_2.A, R2.Pin_1
  N33: LED_3.A, R3.Pin_1
  N34: LED_4.A, R4.Pin_1
  N35: LED_5.A, R5.Pin_1
  N36: LED_8.A, R8.Pin_1
  N37: LED_7.A, R6.Pin_1
  N38: LED_6.A, R7.Pin_1
  N39: LED_Edit.A, R9.Pin_1
  N40: LED_Bypass.A, R10.Pin_1
  N41: U2.MAIN, U20.RIGHT
  N42: U2.NO, U3.NC, U5.MAIN
  N43: U3.MAIN, U34.RIGHT
  N44: U3.NO, U17.RIGHT
  N45: U4.MAIN, U23.RIGHT
  N46: U4.NO, U5.NC, U7.MAIN
  N47: U5.NO, U16.RIGHT
  N48: U6.MAIN, U22.RIGHT
  N49: U6.NO, U7.NC, U9.MAIN
  N50: U7.NO, U15.RIGHT
  N51: U8.MAIN, U19.RIGHT
  N52: U8.NO, U9.NC, U33.MAIN
  N53: U9.NO, U14.RIGHT
  N54: U10.RIGHT, U27.NO
  N55: U11.RIGHT, U28.NO
  N56: U12.RIGHT, U29.NO
  N57: U13.RIGHT, U33.NO
  N58: U18.RIGHT, U31.MAIN
  N59: U21.RIGHT, U30.MAIN
  N60: U24.RIGHT, U32.MAIN
  N61: U25.RIGHT, U26.MAIN
  N62: U26.NO, U29.MAIN, U33.NC
  N63: U27.MAIN, U28.NC, U32.NO
  N64: U27.NC, U31.NO, U35.RIGHT
  N65: U28.MAIN, U29.NC, U30.NO

notes:
  Send Relays
  Return Relays
